// Logisim project FD_group16.circ as structural Verilog: 6 circuits, main circuit main
module main (
  output [11:0] pc,
  output [11:0] r0,
  output [11:0] r1,
  output [11:0] r2,
  output [11:0] r3,
  output [11:0] r4,
  output [11:0] r5,
  output [11:0] r6,
  output [11:0] r7,
  output [11:0] r8,
  output [11:0] r9,
  output [11:0] r10,
  output [11:0] r11,
  output [11:0] r12,
  output [11:0] r13,
  output [11:0] r14,
  output [11:0] r15,
  output halt
);

  wire and_1_out, and_2_out, and_3_out, and_4_out, clock_1_out, control_unit_1_absoltue_branch,
       control_unit_1_addressource, control_unit_1_dont_write_register, control_unit_1_load_12_bit_immediate,
       control_unit_1_load_ram, control_unit_1_relative_branch, control_unit_1_store_programm_counter,
       control_unit_1_store_ram, d_ff_1_q, halt_1_halt, n12_bit_alu_1_overflow, not_1_out, not_2_out,
       reset_out, xor_1_out;
  wire [0:0] control_unit_1_branch_value_choice;
  wire [1:0] control_unit_1_rt_rs_source, or_2_out;
  wire [3:0] control_unit_1__4bit_immediate, control_unit_1_alu_operation, control_unit_1_readfrom_rs,
       control_unit_1_readfrom_rt, control_unit_1_writeto;
  wire [11:0] bit_extender_1_out, control_unit_1__12bit_immediate, modified_register_1_rsource_2,
       modified_register_1_rtarget_2, multiplexer_1_out, multiplexer_2_out, multiplexer_3_out,
       multiplexer_4_out, multiplexer_5_out, multiplexer_6_out, multiplexer_7_out, n12_bit_alu_1_result,
       ram_2_data;
  wire [15:0] ram_1_data;

  Halt halt_1 (.instruction(ram_1_data), .klok(clock_1_out), .reset(reset_out), .halt(halt_1_halt));
  Clock clock_1 (.out(clock_1_out));
  Button reset (.out(reset_out));
  or or_1 (halt, halt_1_halt, d_ff_1_q);
  and and_1 (and_1_out, ~halt, clock_1_out);  // AND_Gate
  D_Flip_Flop #(.trigger("falling")) d_ff_1 (
    .clk(and_1_out), .D(n12_bit_alu_1_overflow), .Q(d_ff_1_q));  // open: Qn, preset, en, reset
  Multiplexer #(.select(2), .width(12)) multiplexer_1 (
    .in0({12{1'b0}}), .in1(control_unit_1__12bit_immediate), .in2(multiplexer_5_out),
    .out(multiplexer_1_out), .sel(or_2_out));  // open: in3, en
  or or_2 (or_2_out[0], and_2_out, and_3_out);
  modified_counter modified_counter_1 (
    .branch_value(multiplexer_1_out), .klok(and_1_out), .reset(reset_out),
    .relative_branch(control_unit_1_relative_branch), .absolute_branch(control_unit_1_absoltue_branch),
    .out_6(pc));
  and and_2 (and_2_out, control_unit_1_branch_value_choice[0], and_4_out);
  and and_3 (and_3_out, control_unit_1_branch_value_choice[0], control_unit_1_absoltue_branch);
  and and_4 (and_4_out, xor_1_out, control_unit_1_relative_branch);
  RAM #(.addrWidth(12), .dataWidth(16), .bus("separate")) ram_1 (
    .addr(pc), .din(ram_1_data), .data(ram_1_data), .sel(1'b1), .clk(and_1_out), .clr(reset_out));  // open: str, ld
  xor xor_1 (xor_1_out, 1'b1, multiplexer_5_out[0]);
  control_unit control_unit_1 (
    .operation(ram_1_data), .dont_write_register(control_unit_1_dont_write_register),
    .rt_rs_source(control_unit_1_rt_rs_source), .store_ram(control_unit_1_store_ram),
    .load_ram(control_unit_1_load_ram), .alu_operation(control_unit_1_alu_operation),
    .relative_branch(control_unit_1_relative_branch), .addressource(control_unit_1_addressource),
    .load_12_bit_immediate(control_unit_1_load_12_bit_immediate),
    .absoltue_branch(control_unit_1_absoltue_branch),
    .store_programm_counter(control_unit_1_store_programm_counter), .writeto(control_unit_1_writeto),
    .readfrom_rs(control_unit_1_readfrom_rs), .readfrom_rt(control_unit_1_readfrom_rt),
    ._12bit_immediate(control_unit_1__12bit_immediate), ._4bit_immediate(control_unit_1__4bit_immediate),
    .branch_value_choice({or_2_out[1], control_unit_1_branch_value_choice[0]}));  // open: get_rt_or_rs
  Multiplexer #(.width(12)) multiplexer_2 (
    .in0(multiplexer_5_out), .in1(n12_bit_alu_1_result), .out(multiplexer_2_out),
    .sel(control_unit_1_store_programm_counter));  // open: en
  modified_register modified_register_1 (
    .data(multiplexer_2_out), .write(not_1_out), .klok(and_1_out), .reset(reset_out),
    .rdestination(control_unit_1_writeto), .rtarget(control_unit_1_readfrom_rt),
    .rSource(control_unit_1_readfrom_rs), .rsource_2(modified_register_1_rsource_2),
    .rtarget_2(modified_register_1_rtarget_2), .out_10(r0), .out_11(r1), .out_12(r2), .out_13(r3),
    .out_14(r4), .out_15(r5), .out_16(r6), .out_17(r7), .out_18(r8), .out_19(r9), .out_20(r10), .out_21(r11),
    .out_22(r12), .out_23(r13), .out_24(r14), .out_25(r15));
  not not_1 (not_1_out, control_unit_1_dont_write_register);
  assign bit_extender_1_out = {{8{1'b0}}, control_unit_1__4bit_immediate};  // Bit_Extender bit_extender_1
  Multiplexer #(.select(2), .width(12)) multiplexer_3 (
    .in0(modified_register_1_rsource_2), .in1(modified_register_1_rsource_2),
    .in2(modified_register_1_rsource_2), .in3(12'h1), .out(multiplexer_3_out),
    .sel(control_unit_1_rt_rs_source));  // open: en
  Multiplexer #(.width(12)) multiplexer_4 (
    .in0(ram_2_data), .in1(n12_bit_alu_1_result), .out(multiplexer_4_out), .sel(not_2_out));  // open: en
  Multiplexer #(.width(12)) multiplexer_5 (
    .in0(multiplexer_4_out), .in1(control_unit_1__12bit_immediate), .out(multiplexer_5_out),
    .sel(control_unit_1_load_12_bit_immediate));  // open: en
  Multiplexer #(.select(2), .width(12)) multiplexer_6 (
    .in0(modified_register_1_rtarget_2), .in1(bit_extender_1_out), .in2(control_unit_1__12bit_immediate),
    .in3(pc), .out(multiplexer_6_out), .sel(control_unit_1_rt_rs_source));  // open: en
  not not_2 (not_2_out, control_unit_1_load_ram);
  _12_bit_ALU u_12_bit_alu_1 (
    .ALU_code(control_unit_1_alu_operation), .a(multiplexer_3_out), .b(multiplexer_6_out),
    .overflow(n12_bit_alu_1_overflow), .result(n12_bit_alu_1_result));
  Multiplexer #(.width(12)) multiplexer_7 (
    .in0({12{1'b0}}), .in1(modified_register_1_rtarget_2), .out(multiplexer_7_out),
    .sel(control_unit_1_addressource));  // open: en
  RAM #(.addrWidth(12), .dataWidth(12), .bus("separate")) ram_2 (
    .addr(n12_bit_alu_1_result), .din(multiplexer_7_out), .data(ram_2_data), .str(control_unit_1_store_ram),
    .clk(and_1_out), .ld(control_unit_1_load_ram), .clr(reset_out));  // open: sel

  // Notes on the sheet:
  //   current instruction
  //   clock signal
  //   reset button
  //   DO NOT CHANGE THE INPUTS AND OUTPUTS OF THIS CIRCUIT! Do not add/remove inputs or outputs. Do not even change their location or orientation.
  //   overflow van de alu-bewerking
endmodule

module Halt (
  input  [15:0] instruction,
  input  klok,
  input  reset,
  output halt
);

  wire and_1_out, comparator_1_eq, comparator_2_gt, counter_1_carry, or_1_out, or_2_out;
  wire [11:0] counter_1_q;

  Counter #(.width(12), .max('hfff), .trigger("falling")) counter_1 (
    .Q(counter_1_q), .carry(counter_1_carry), .clk(klok), .clr(reset));  // open: load, D, count
  Comparator #(.width(16), .mode("unsigned")) comparator_1 (
    .a(instruction), .b({16{1'b0}}), .eq(comparator_1_eq));  // open: gt, lt
  or or_1 (or_1_out, comparator_1_eq, counter_1_carry);
  Comparator #(.width(12), .mode("unsigned")) comparator_2 (
    .a(counter_1_q), .b({12{1'b0}}), .gt(comparator_2_gt));  // open: eq, lt
  or or_2 (or_2_out, halt, and_1_out);
  and and_1 (and_1_out, or_1_out, comparator_2_gt);
  Register #(.width(1)) register_1 (.D(or_2_out), .Q(halt), .clk(klok), .clr(reset));  // open: en

  // Notes on the sheet:
  //   halt becomes and stays asserted if the instruction is 0000 (not in the first clock cycle) or the end of the counter is reached (2^12)
endmodule

module programm_counter (
  input  reset,
  input  branch_relative,
  input  branch_abslolute,
  input  [11:0] branch_value,
  input  klok,
  output [11:0] \output 
);

  wire and_1_out, not_1_out;

  not not_1 (not_1_out, branch_relative);
  and and_1 (and_1_out, not_1_out, branch_abslolute);
  modified_counter modified_counter_1 (
    .branch_value(branch_value), .klok(klok), .reset(reset), .relative_branch(branch_relative),
    .absolute_branch(and_1_out), .out_6(\output ));
endmodule

module modified_counter (
  input  relative_branch,
  input  reset,
  input  absolute_branch,
  input  [11:0] branch_value,
  input  klok,
  output [11:0] out_6
);

  wire [1:0] or_2_out;
  wire [11:0] multiplexer_1_out, n12_bit_carry_lookahead_adder_1_out_4, n12_bit_carry_lookahead_adder_2_out_4;

  _12_bit_carry_lookahead__adder u_12_bit_carry_lookahead_adder_1 (
    .in_1(out_6), .in_3({12{1'b0}}), .out_4(n12_bit_carry_lookahead_adder_1_out_4), .carryin(1'b1));  // open: overflow
  or or_1 (or_2_out[1], relative_branch, reset);
  _12_bit_carry_lookahead__adder u_12_bit_carry_lookahead_adder_2 (
    .in_1(n12_bit_carry_lookahead_adder_1_out_4), .in_3(branch_value),
    .out_4(n12_bit_carry_lookahead_adder_2_out_4), .carryin(1'b0));  // open: overflow
  or or_2 (or_2_out[0], reset, absolute_branch);
  Multiplexer #(.select(2), .width(12)) multiplexer_1 (
    .in0(n12_bit_carry_lookahead_adder_1_out_4), .in1(branch_value),
    .in2(n12_bit_carry_lookahead_adder_2_out_4), .in3({12{1'b0}}), .out(multiplexer_1_out), .sel(or_2_out));  // open: en
  _12_bit_register u_12_bit_register_1 (
    .Q(out_6), .D(multiplexer_1_out), .reset(reset), .clock(klok));  // open: enable_write
endmodule

module modified_register (
  input  [3:0] rdestination,
  input  [3:0] rSource,
  input  [11:0] data,
  input  write,
  input  klok,
  input  reset,
  input  [3:0] rtarget,
  output [11:0] rsource_2,
  output [11:0] rtarget_2,
  output [11:0] out_10,
  output [11:0] out_11,
  output [11:0] out_12,
  output [11:0] out_13,
  output [11:0] out_14,
  output [11:0] out_15,
  output [11:0] out_16,
  output [11:0] out_17,
  output [11:0] out_18,
  output [11:0] out_19,
  output [11:0] out_20,
  output [11:0] out_21,
  output [11:0] out_22,
  output [11:0] out_23,
  output [11:0] out_24,
  output [11:0] out_25
);

  wire demultiplexer_1_out0, demultiplexer_1_out1, demultiplexer_1_out2, demultiplexer_1_out3,
       demultiplexer_1_out4, demultiplexer_1_out5, demultiplexer_1_out6, demultiplexer_1_out7,
       demultiplexer_1_out8, demultiplexer_1_out9, demultiplexer_1_out10, demultiplexer_1_out11,
       demultiplexer_1_out12, demultiplexer_1_out13, demultiplexer_1_out14, demultiplexer_1_out15;

  Demultiplexer #(.select(4)) demultiplexer_1 (
    .out0(demultiplexer_1_out0), .out1(demultiplexer_1_out1), .out2(demultiplexer_1_out2),
    .out3(demultiplexer_1_out3), .out4(demultiplexer_1_out4), .out5(demultiplexer_1_out5),
    .out6(demultiplexer_1_out6), .out7(demultiplexer_1_out7), .out8(demultiplexer_1_out8),
    .out9(demultiplexer_1_out9), .out10(demultiplexer_1_out10), .out11(demultiplexer_1_out11),
    .out12(demultiplexer_1_out12), .out13(demultiplexer_1_out13), .out14(demultiplexer_1_out14),
    .out15(demultiplexer_1_out15), .in(write), .sel(rdestination));  // open: en
  _12_bit_register u_12_bit_register_1 (
    .Q(out_10), .D(data), .reset(1'b1), .enable_write(demultiplexer_1_out0), .clock(klok));
  _12_bit_register u_12_bit_register_2 (
    .Q(out_11), .D(data), .reset(reset), .enable_write(demultiplexer_1_out1), .clock(klok));
  _12_bit_register u_12_bit_register_3 (
    .Q(out_12), .D(data), .reset(reset), .enable_write(demultiplexer_1_out2), .clock(klok));
  _12_bit_register u_12_bit_register_4 (
    .Q(out_13), .D(data), .reset(reset), .enable_write(demultiplexer_1_out3), .clock(klok));
  _12_bit_register u_12_bit_register_5 (
    .Q(out_14), .D(data), .reset(reset), .enable_write(demultiplexer_1_out4), .clock(klok));
  _12_bit_register u_12_bit_register_6 (
    .Q(out_15), .D(data), .reset(reset), .enable_write(demultiplexer_1_out5), .clock(klok));
  _12_bit_register u_12_bit_register_7 (
    .Q(out_16), .D(data), .reset(reset), .enable_write(demultiplexer_1_out6), .clock(klok));
  _12_bit_register u_12_bit_register_8 (
    .Q(out_17), .D(data), .reset(reset), .enable_write(demultiplexer_1_out7), .clock(reset));
  _12_bit_register u_12_bit_register_9 (
    .Q(out_18), .D(data), .reset(reset), .enable_write(demultiplexer_1_out8), .clock(klok));
  _12_bit_register u_12_bit_register_10 (
    .Q(out_19), .D(data), .reset(reset), .enable_write(demultiplexer_1_out9), .clock(klok));
  _12_bit_register u_12_bit_register_11 (
    .Q(out_20), .D(data), .reset(reset), .enable_write(demultiplexer_1_out10), .clock(klok));
  _12_bit_register u_12_bit_register_12 (
    .Q(out_21), .D(data), .reset(reset), .enable_write(demultiplexer_1_out11), .clock(klok));
  _12_bit_register u_12_bit_register_13 (
    .Q(out_22), .D(data), .reset(reset), .enable_write(demultiplexer_1_out12), .clock(klok));
  _12_bit_register u_12_bit_register_14 (
    .Q(out_23), .D(data), .reset(reset), .enable_write(demultiplexer_1_out13), .clock(klok));
  _12_bit_register u_12_bit_register_15 (
    .Q(out_24), .D(data), .reset(reset), .enable_write(demultiplexer_1_out14), .clock(klok));
  _12_bit_register u_12_bit_register_16 (
    .Q(out_25), .D(data), .reset(reset), .enable_write(demultiplexer_1_out15), .clock(klok));
  Multiplexer #(.select(4), .width(12)) multiplexer_1 (
    .in0(out_10), .in1(out_11), .in2(out_12), .in3(out_13), .in4(out_14), .in5(out_15), .in6(out_16),
    .in7(out_17), .in8(out_18), .in9(out_19), .in10(out_20), .in11(out_21), .in12(out_22), .in13(out_23),
    .in14(out_24), .in15(out_25), .out(rsource_2), .sel(rSource));  // open: en
  Multiplexer #(.select(4), .width(12)) multiplexer_2 (
    .in0(out_10), .in1(out_11), .in2(out_12), .in3(out_13), .in4(out_14), .in5(out_15), .in6(out_16),
    .in7(out_17), .in8(out_18), .in9(out_19), .in10(out_20), .in11(out_21), .in12(out_22), .in13(out_23),
    .in14(out_24), .in15(out_25), .out(rtarget_2), .sel(rtarget));  // open: en
endmodule

module control_unit (
  input  [15:0] operation,
  output [3:0] writeto,
  output [3:0] readfrom_rs,
  output [3:0] readfrom_rt,
  output [11:0] _12bit_immediate,
  output [3:0] _4bit_immediate,
  output dont_write_register,
  output get_rt_or_rs,
  output [1:0] rt_rs_source,
  output store_ram,
  output load_ram,
  output [3:0] alu_operation,
  output relative_branch,
  output addressource,
  output load_12_bit_immediate,
  output absoltue_branch,
  output store_programm_counter,
  output [1:0] branch_value_choice
);

  wire and_1_out, comparator_4_eq, comparator_5_eq, comparator_6_eq, comparator_7_eq, comparator_8_eq,
       or_4_out;
  wire [0:0] or_1_out;
  wire [1:0] multiplexer_4_out, or_8_out, or_10_out;
  wire [11:0] bit_extender_1_out, bit_extender_2_out, bit_extender_3_out;

  Comparator #(.width(4)) comparator_1 (.a(operation[15:12]), .b(4'b1101), .eq(store_ram));  // open: gt, lt
  Comparator #(.width(4)) comparator_2 (.a(operation[15:12]), .b(4'b1100), .eq(load_ram));  // open: gt, lt
  Comparator #(.width(4)) comparator_3 (.a(operation[15:12]), .b(4'b1110), .eq(relative_branch));  // open: gt, lt
  Comparator #(.width(4)) comparator_4 (.a(operation[15:12]), .b(4'b1111), .eq(comparator_4_eq));  // open: gt, lt
  Comparator #(.width(2)) comparator_5 (.a(operation[1:0]), .b(2'b00), .eq(comparator_5_eq));  // open: gt, lt
  Comparator #(.width(2)) comparator_6 (.a(operation[1:0]), .b(2'b01), .eq(comparator_6_eq));  // open: gt, lt
  Comparator #(.width(2)) comparator_7 (.a(operation[1:0]), .b(2'b10), .eq(comparator_7_eq));  // open: gt, lt
  Comparator #(.width(2)) comparator_8 (.a(operation[1:0]), .b(2'b11), .eq(comparator_8_eq));  // open: gt, lt
  Multiplexer #(.width(4)) multiplexer_1 (
    .in0(operation[11:8]), .in1(4'b1111), .out(writeto), .sel(store_programm_counter));  // open: en
  and and_1 (and_1_out, comparator_4_eq, comparator_5_eq);
  and and_2 (load_12_bit_immediate, comparator_4_eq, comparator_6_eq);
  and and_3 (branch_value_choice[1], comparator_4_eq, comparator_7_eq);
  and and_4 (store_programm_counter, comparator_4_eq, comparator_8_eq);
  Multiplexer #(.select(2), .width(4)) multiplexer_2 (
    .in0(operation[7:4]), .in1(operation[11:8]), .in2(operation[3:0]), .out(readfrom_rs),
    .sel({1'b0, or_1_out[0]}));  // open: in3, en
  or or_1 (or_1_out[0], and_1_out, branch_value_choice[1]);
  Multiplexer #(.select(2), .width(4)) multiplexer_3 (
    .in0(operation[3:0]), .in1(operation[7:4]), .in2(operation[11:8]), .out(readfrom_rt),
    .sel(multiplexer_4_out));  // open: in3, en
  Multiplexer #(.width(2)) multiplexer_4 (
    .in0(2'b00), .in1(2'b10), .out(multiplexer_4_out), .sel(get_rt_or_rs));  // open: en
  or or_2 (dont_write_register, store_ram, branch_value_choice[1], relative_branch);
  or or_3 (get_rt_or_rs, store_ram, relative_branch);
  or or_4 (or_4_out, store_ram, load_ram, branch_value_choice[1]);
  or or_5 (addressource, store_ram, load_ram);
  or or_6 (absoltue_branch, branch_value_choice[1], store_programm_counter);
  or or_7 (branch_value_choice[0], relative_branch, store_programm_counter);
  or or_8 (or_8_out[0], or_4_out, store_programm_counter, and_1_out);
  or or_9 (or_8_out[1], and_1_out, relative_branch);
  Multiplexer #(.select(2), .width(12)) multiplexer_5 (
    .in0(bit_extender_1_out), .in1({operation[7:2], {6{1'b0}}}), .in2(bit_extender_3_out),
    .in3(bit_extender_2_out), .out(_12bit_immediate), .sel(or_10_out));  // open: en
  assign bit_extender_1_out = {{6{1'b0}}, operation[7:2]};  // Bit_Extender bit_extender_1
  or or_10 (or_10_out[0], relative_branch, load_12_bit_immediate);
  or or_11 (rt_rs_source[0], store_ram, store_programm_counter, load_ram);
  or or_12 (rt_rs_source[1], and_1_out, store_programm_counter, branch_value_choice[1]);
  Multiplexer #(.select(2), .width(4)) multiplexer_6 (
    .in0(operation[15:12]), .in1(4'b0101), .in2(4'b1011), .in3(4'b0010), .out(alu_operation), .sel(or_8_out));  // open: en
  or or_13 (or_10_out[1], store_programm_counter, relative_branch);
  assign bit_extender_2_out = {{8{1'b0}}, operation[3:0]};  // Bit_Extender bit_extender_2
  assign bit_extender_3_out = {{2{1'b0}}, operation[11:2]};  // Bit_Extender bit_extender_3

  assign _4bit_immediate = operation[3:0];

  // Notes on the sheet:
  //   store word
  //   load word
  //   branch not equal
  //   ori
  //   lui
  //   jr 
  //   jal
  //   immediate circuit
endmodule
