// Logisim project project2.circ as structural Verilog
module oef2_1 (
  input  [1:0] in_1,
  output O0,
  output O1,
  output O2,
  output O3
);

  wire not_1_out, not_2_out, or_1_out;

  not not_1 (not_1_out, in_1[1]);
  not not_2 (not_2_out, in_1[0]);
  or or_1 (or_1_out, in_1[0], in_1[1]);
  not not_3 (O0, or_1_out);
  and and_1 (O1, in_1[0], not_1_out);
  and and_2 (O2, not_2_out, in_1[1]);
  and and_3 (O3, in_1[1], in_1[0]);

  // Notes on the sheet:
  //   b0
  //   b1
endmodule

module oef2_2 (
  input  [1:0] input_0,
  input  [1:0] input_1,
  input  [1:0] input_2,
  input  [1:0] input_3,
  input  [1:0] selector,
  output [1:0] \output 
);

  wire [1:0] and_1_out, and_2_out, and_3_out, and_4_out;
  wire [1:1] oef2_1_1_o0, oef2_1_1_o1, oef2_1_1_o2, oef2_1_1_o3;

  oef2_1 oef2_1_1 (.in_1(selector), .O0(oef2_1_1_o0[1]), .O1(oef2_1_1_o1[1]), .O2(oef2_1_1_o2[1]), .O3(oef2_1_1_o3[1]));
  assign and_1_out = input_0 & {2{oef2_1_1_o0[1]}};  // AND_Gate and_1, 2 bits wide
  assign and_2_out = input_1 & {2{oef2_1_1_o1[1]}};  // AND_Gate and_2, 2 bits wide
  assign and_3_out = input_2 & {2{oef2_1_1_o2[1]}};  // AND_Gate and_3, 2 bits wide
  assign and_4_out = input_3 & {2{oef2_1_1_o3[1]}};  // AND_Gate and_4, 2 bits wide
  assign \output  = and_1_out | and_2_out | and_3_out | and_4_out;  // OR_Gate or_1, 2 bits wide
endmodule

module oude_1_bit_adder (
  input  Ci,
  input  I1,
  input  I2,
  output O,
  output Co
);

  wire and_1_out, and_2_out, and_3_out, and_4_out, and_5_out, not_1_out, not_2_out, not_3_out, or_1_out,
       or_3_out;

  or or_1 (or_1_out, I1, I2);
  and and_1 (and_1_out, I1, I2);
  and and_2 (and_2_out, Ci, or_1_out);
  or or_2 (Co, and_2_out, and_1_out);
  not not_1 (not_1_out, and_1_out);
  and and_3 (and_3_out, or_1_out, not_1_out);
  not not_2 (not_2_out, or_1_out);
  or or_3 (or_3_out, and_1_out, not_2_out);
  not not_3 (not_3_out, Ci);
  and and_4 (and_4_out, not_3_out, and_3_out);
  and and_5 (and_5_out, Ci, or_3_out);
  or or_4 (O, and_4_out, and_5_out);
endmodule

module _4_bit_carry_lookahead_block (
  input  c0,
  input  a0,
  input  b0,
  input  a1,
  input  b1,
  input  a2,
  input  b2,
  input  a3,
  input  b3,
  output C1,
  output C2,
  output C3,
  output C4,
  output P0,
  output G0
);

  wire and_1_out, and_2_out, and_3_out, and_4_out, and_6_out, and_7_out, and_8_out, and_9_out, and_10_out,
       and_11_out, and_12_out, and_13_out, and_14_out, and_15_out, or_1_out, or_2_out, or_3_out, or_4_out;

  and and_1 (and_1_out, a0, b0);
  or or_1 (or_1_out, a0, a0, b0);
  and and_2 (and_2_out, a1, b1);
  or or_2 (or_2_out, a1, b1);
  and and_3 (and_3_out, a2, b2);
  or or_3 (or_3_out, a2, b2);
  and and_4 (and_4_out, a3, b3);
  or or_4 (or_4_out, a3, b3);
  and and_5 (P0, or_1_out, or_2_out, or_3_out, or_4_out);
  and and_6 (and_6_out, c0, or_1_out);
  and and_7 (and_7_out, and_3_out, or_4_out);
  and and_8 (and_8_out, and_2_out, or_4_out, or_3_out);
  or or_5 (C1, and_1_out, and_6_out);
  and and_9 (and_9_out, or_1_out, c0, or_2_out);
  and and_10 (and_10_out, and_1_out, or_2_out);
  and and_11 (and_11_out, and_2_out, or_3_out);
  and and_12 (and_12_out, and_1_out, or_3_out, or_2_out);
  and and_13 (and_13_out, or_3_out, or_2_out, or_1_out, c0);
  and and_14 (and_14_out, and_1_out, or_4_out, or_3_out, or_2_out);
  and and_15 (and_15_out, or_1_out, or_4_out, or_3_out, or_2_out, c0);
  or or_6 (C2, and_2_out, and_9_out, and_10_out);
  or or_7 (G0, and_7_out, and_14_out, and_8_out, and_4_out);
  or or_8 (C4, and_4_out, and_7_out, and_8_out, and_14_out, and_15_out);
  or or_9 (C3, and_3_out, and_11_out, and_12_out, and_13_out);
endmodule

module _12_bit_ripple_carry_adder (
  input  Ci,
  input  [11:0] I0,
  input  [11:0] I1,
  output [11:0] O,
  output C0,
  output overflow
);

  wire and_1_out, and_2_out, n1_bit_adder_1_co, n1_bit_adder_2_co, n1_bit_adder_3_co, n1_bit_adder_4_co,
       n1_bit_adder_5_co, n1_bit_adder_6_co, n1_bit_adder_7_co, n1_bit_adder_8_co, n1_bit_adder_9_co,
       n1_bit_adder_10_co, n1_bit_adder_11_co, not_1_out, not_2_out;

  _1_bit_adder u_1_bit_adder_1 (.I1(I1[0]), .I2(I0[0]), .Ci(Ci), .Co(n1_bit_adder_1_co), .O(O[0]));
  _1_bit_adder u_1_bit_adder_2 (.I1(I1[1]), .I2(I0[1]), .Ci(n1_bit_adder_1_co), .Co(n1_bit_adder_2_co), .O(O[1]));
  _1_bit_adder u_1_bit_adder_3 (.I1(I1[2]), .I2(I0[2]), .Ci(n1_bit_adder_2_co), .Co(n1_bit_adder_3_co), .O(O[2]));
  _1_bit_adder u_1_bit_adder_4 (.I1(I1[3]), .I2(I0[3]), .Ci(n1_bit_adder_3_co), .Co(n1_bit_adder_4_co), .O(O[3]));
  _1_bit_adder u_1_bit_adder_5 (.I1(I1[4]), .I2(I0[4]), .Ci(n1_bit_adder_4_co), .Co(n1_bit_adder_5_co), .O(O[4]));
  _1_bit_adder u_1_bit_adder_6 (.I1(I1[5]), .I2(I0[5]), .Ci(n1_bit_adder_5_co), .Co(n1_bit_adder_6_co), .O(O[5]));
  _1_bit_adder u_1_bit_adder_7 (.I1(I1[6]), .I2(I0[6]), .Ci(n1_bit_adder_6_co), .Co(n1_bit_adder_7_co), .O(O[6]));
  _1_bit_adder u_1_bit_adder_8 (.I1(I1[7]), .I2(I0[7]), .Ci(n1_bit_adder_7_co), .Co(n1_bit_adder_8_co), .O(O[7]));
  _1_bit_adder u_1_bit_adder_9 (.I1(I1[8]), .I2(I0[8]), .Ci(n1_bit_adder_8_co), .Co(n1_bit_adder_9_co), .O(O[8]));
  _1_bit_adder u_1_bit_adder_10 (.I1(I1[9]), .I2(I0[9]), .Ci(n1_bit_adder_9_co), .Co(n1_bit_adder_10_co), .O(O[9]));
  _1_bit_adder u_1_bit_adder_11 (.I1(I1[10]), .I2(I0[10]), .Ci(n1_bit_adder_10_co), .Co(n1_bit_adder_11_co), .O(O[10]));
  _1_bit_adder u_1_bit_adder_12 (.I1(I1[11]), .I2(I0[11]), .Ci(n1_bit_adder_11_co), .Co(C0), .O(O[11]));
  not not_1 (not_1_out, C0);
  not not_2 (not_2_out, n1_bit_adder_11_co);
  and and_1 (and_1_out, n1_bit_adder_11_co, not_1_out);
  and and_2 (and_2_out, not_2_out, C0);
  or or_1 (overflow, and_1_out, and_2_out);
endmodule

module _12_bit_carry_lookahead__adder (
  input  [11:0] in_1,
  input  carryin,
  input  [11:0] in_3,
  output [11:0] out_4,
  output overflow
);

  wire and_1_out, and_2_out, and_3_out, and_4_out, and_5_out, and_6_out, n4_bit_carry_lookahead_block_1_c1,
       n4_bit_carry_lookahead_block_1_c2, n4_bit_carry_lookahead_block_1_c3,
       n4_bit_carry_lookahead_block_1_c4, n4_bit_carry_lookahead_block_1_g0,
       n4_bit_carry_lookahead_block_1_p0, n4_bit_carry_lookahead_block_2_c1,
       n4_bit_carry_lookahead_block_2_c2, n4_bit_carry_lookahead_block_2_c3,
       n4_bit_carry_lookahead_block_2_c4, n4_bit_carry_lookahead_block_2_g0,
       n4_bit_carry_lookahead_block_2_p0, n4_bit_carry_lookahead_block_3_c1,
       n4_bit_carry_lookahead_block_3_c2, n4_bit_carry_lookahead_block_3_c3,
       n4_bit_carry_lookahead_block_3_c4, n4_bit_carry_lookahead_block_3_g0,
       n4_bit_carry_lookahead_block_3_p0, or_1_out, or_2_out;

  _4_bit_carry_lookahead_block u_4_bit_carry_lookahead_block_1 (
    .a0(in_1[0]), .b0(in_3[0]), .a1(in_1[1]), .b1(in_3[1]), .a2(in_1[2]), .b2(in_3[2]), .a3(in_1[3]),
    .b3(in_3[3]), .C1(n4_bit_carry_lookahead_block_1_c1), .C2(n4_bit_carry_lookahead_block_1_c2),
    .C3(n4_bit_carry_lookahead_block_1_c3), .C4(n4_bit_carry_lookahead_block_1_c4), .c0(carryin),
    .P0(n4_bit_carry_lookahead_block_1_p0), .G0(n4_bit_carry_lookahead_block_1_g0));
  _4_bit_carry_lookahead_block u_4_bit_carry_lookahead_block_2 (
    .a0(in_1[4]), .b0(in_3[4]), .a1(in_1[5]), .b1(in_3[5]), .a2(in_1[6]), .b2(in_3[6]), .a3(in_1[7]),
    .b3(in_3[7]), .C1(n4_bit_carry_lookahead_block_2_c1), .C2(n4_bit_carry_lookahead_block_2_c2),
    .C3(n4_bit_carry_lookahead_block_2_c3), .C4(n4_bit_carry_lookahead_block_2_c4), .c0(or_1_out),
    .P0(n4_bit_carry_lookahead_block_2_p0), .G0(n4_bit_carry_lookahead_block_2_g0));
  _4_bit_carry_lookahead_block u_4_bit_carry_lookahead_block_3 (
    .a0(in_1[8]), .b0(in_3[8]), .a1(in_1[9]), .b1(in_3[9]), .a2(in_1[10]), .b2(in_3[10]), .a3(in_1[11]),
    .b3(in_3[11]), .C1(n4_bit_carry_lookahead_block_3_c1), .C2(n4_bit_carry_lookahead_block_3_c2),
    .C3(n4_bit_carry_lookahead_block_3_c3), .C4(n4_bit_carry_lookahead_block_3_c4), .c0(or_2_out),
    .P0(n4_bit_carry_lookahead_block_3_p0), .G0(n4_bit_carry_lookahead_block_3_g0));
  and and_1 (and_1_out, carryin, n4_bit_carry_lookahead_block_1_p0);
  or or_1 (or_1_out, and_1_out, n4_bit_carry_lookahead_block_1_g0);
  and and_2 (and_2_out, n4_bit_carry_lookahead_block_1_g0, n4_bit_carry_lookahead_block_2_p0);
  and and_3 (and_3_out, n4_bit_carry_lookahead_block_2_g0, n4_bit_carry_lookahead_block_3_p0);
  and and_4 (and_4_out, n4_bit_carry_lookahead_block_2_p0, n4_bit_carry_lookahead_block_3_p0, n4_bit_carry_lookahead_block_1_g0);
  and and_5 (and_5_out, n4_bit_carry_lookahead_block_3_p0, n4_bit_carry_lookahead_block_2_p0, n4_bit_carry_lookahead_block_1_p0, carryin);
  and and_6 (and_6_out, n4_bit_carry_lookahead_block_1_p0, carryin, n4_bit_carry_lookahead_block_2_p0);
  or or_2 (or_2_out, and_2_out, and_6_out, n4_bit_carry_lookahead_block_2_g0);
  or or_3 (overflow, n4_bit_carry_lookahead_block_3_g0, and_3_out, and_4_out, and_5_out);
  _1_bit_full_adder_zonder_carryOut u_1_bit_full_adder_zonder_carryout_1 (
    .I1(in_1[0]), .I2(in_3[0]), .Ci(carryin), .O(out_4[0]));
  _1_bit_full_adder_zonder_carryOut u_1_bit_full_adder_zonder_carryout_2 (
    .I1(in_1[1]), .I2(in_3[1]), .Ci(n4_bit_carry_lookahead_block_1_c1), .O(out_4[1]));
  _1_bit_full_adder_zonder_carryOut u_1_bit_full_adder_zonder_carryout_3 (
    .I1(in_1[2]), .I2(in_3[2]), .Ci(n4_bit_carry_lookahead_block_1_c2), .O(out_4[2]));
  _1_bit_full_adder_zonder_carryOut u_1_bit_full_adder_zonder_carryout_4 (
    .I1(in_1[3]), .I2(in_3[3]), .Ci(n4_bit_carry_lookahead_block_1_c3), .O(out_4[3]));
  _1_bit_full_adder_zonder_carryOut u_1_bit_full_adder_zonder_carryout_5 (
    .I1(in_1[4]), .I2(in_3[4]), .Ci(n4_bit_carry_lookahead_block_1_c4), .O(out_4[4]));
  _1_bit_full_adder_zonder_carryOut u_1_bit_full_adder_zonder_carryout_6 (
    .I1(in_1[5]), .I2(in_3[5]), .Ci(n4_bit_carry_lookahead_block_2_c1), .O(out_4[5]));
  _1_bit_full_adder_zonder_carryOut u_1_bit_full_adder_zonder_carryout_7 (
    .I1(in_1[6]), .I2(in_3[6]), .Ci(n4_bit_carry_lookahead_block_2_c2), .O(out_4[6]));
  _1_bit_full_adder_zonder_carryOut u_1_bit_full_adder_zonder_carryout_8 (
    .I1(in_1[7]), .I2(in_3[7]), .Ci(n4_bit_carry_lookahead_block_2_c3), .O(out_4[7]));
  _1_bit_full_adder_zonder_carryOut u_1_bit_full_adder_zonder_carryout_9 (
    .I1(in_1[8]), .I2(in_3[8]), .Ci(n4_bit_carry_lookahead_block_2_c4), .O(out_4[8]));
  _1_bit_full_adder_zonder_carryOut u_1_bit_full_adder_zonder_carryout_10 (
    .I1(in_1[9]), .I2(in_3[9]), .Ci(n4_bit_carry_lookahead_block_3_c1), .O(out_4[9]));
  _1_bit_full_adder_zonder_carryOut u_1_bit_full_adder_zonder_carryout_11 (
    .I1(in_1[10]), .I2(in_3[10]), .Ci(n4_bit_carry_lookahead_block_3_c2), .O(out_4[10]));
  _1_bit_full_adder_zonder_carryOut u_1_bit_full_adder_zonder_carryout_12 (
    .I1(in_1[11]), .I2(in_3[11]), .Ci(n4_bit_carry_lookahead_block_3_c3), .O(out_4[11]));
  _12_bit_ripple_carry_adder u_12_bit_ripple_carry_adder_1 ();  // open: I0, I1, Ci, C0, O, overflow
endmodule

module _1_bit_adder (
  input  Ci,
  input  I1,
  input  I2,
  output O,
  output Co
);

  wire and_1_out, and_2_out, and_3_out, and_4_out, and_5_out, and_6_out, and_7_out, not_1_out, not_2_out,
       not_3_out, not_4_out, not_5_out, not_6_out;

  and and_1 (and_1_out, Ci, I1);
  and and_2 (and_2_out, Ci, I2);
  or or_1 (Co, and_1_out, and_2_out, and_7_out);
  not not_1 (not_1_out, I1);
  not not_2 (not_2_out, I2);
  not not_3 (not_3_out, I1);
  not not_4 (not_4_out, Ci);
  not not_5 (not_5_out, I2);
  not not_6 (not_6_out, Ci);
  and and_3 (and_3_out, not_1_out, not_2_out, Ci);
  and and_4 (and_4_out, not_3_out, I2, not_4_out);
  and and_5 (and_5_out, I1, not_5_out, not_6_out);
  and and_6 (and_6_out, I1, I2, Ci);
  and and_7 (and_7_out, I1, I2);
  or or_2 (O, and_3_out, and_4_out, and_5_out, and_6_out);
endmodule

module _1_bit_full_adder_zonder_carryOut (
  input  Ci,
  input  I1,
  input  I2,
  output O
);

  wire and_1_out, and_2_out, and_3_out, and_4_out, not_1_out, not_2_out, not_3_out, not_4_out, not_5_out,
       not_6_out;

  not not_1 (not_1_out, I1);
  not not_2 (not_2_out, I2);
  not not_3 (not_3_out, I1);
  not not_4 (not_4_out, Ci);
  not not_5 (not_5_out, I2);
  not not_6 (not_6_out, Ci);
  and and_1 (and_1_out, not_1_out, not_2_out, Ci);
  and and_2 (and_2_out, not_3_out, I2, not_4_out);
  and and_3 (and_3_out, I1, not_5_out, not_6_out);
  and and_4 (and_4_out, I1, I2, Ci);
  or or_1 (O, and_1_out, and_2_out, and_3_out, and_4_out);
endmodule

module _4_bit_carry_lookahead (
  input  in_1,
  input  [3:0] in_2,
  input  in_3,
  input  [3:0] in_4,
  output [3:0] out_5
);

  wire n4_bit_carry_lookahead_block_1_c1, n4_bit_carry_lookahead_block_1_c2,
       n4_bit_carry_lookahead_block_1_c3;

  _4_bit_carry_lookahead_block u_4_bit_carry_lookahead_block_1 (
    .a0(in_2[0]), .b0(in_4[0]), .a1(in_2[1]), .b1(in_4[1]), .a2(in_2[2]), .b2(in_4[2]), .a3(in_2[3]),
    .b3(in_4[3]), .C1(n4_bit_carry_lookahead_block_1_c1), .C2(n4_bit_carry_lookahead_block_1_c2),
    .C3(n4_bit_carry_lookahead_block_1_c3), .c0(in_3));  // open: C4, P0, G0
  _1_bit_full_adder_zonder_carryOut u_1_bit_full_adder_zonder_carryout_1 (
    .I1(in_2[0]), .I2(in_4[0]), .Ci(in_1), .O(out_5[0]));
  _1_bit_full_adder_zonder_carryOut u_1_bit_full_adder_zonder_carryout_2 (
    .I1(in_2[1]), .I2(in_4[1]), .Ci(n4_bit_carry_lookahead_block_1_c1), .O(out_5[1]));
  _1_bit_full_adder_zonder_carryOut u_1_bit_full_adder_zonder_carryout_3 (
    .I1(in_2[2]), .I2(in_4[2]), .Ci(n4_bit_carry_lookahead_block_1_c2), .O(out_5[2]));
  _1_bit_full_adder_zonder_carryOut u_1_bit_full_adder_zonder_carryout_4 (
    .I1(in_2[3]), .I2(in_4[3]), .Ci(n4_bit_carry_lookahead_block_1_c3), .O(out_5[3]));
endmodule
