// Logisim project project4.circ as structural Verilog
module register_file (
  input  [3:0] rtarget,
  input  [3:0] rSource,
  input  [11:0] data,
  input  write,
  input  [3:0] rDestination,
  input  reset,
  output [11:0] out_7,
  output [11:0] out_8
);

  wire clock_out, demultiplexer_1_out0, demultiplexer_1_out1, demultiplexer_1_out2, demultiplexer_1_out3,
       demultiplexer_1_out4, demultiplexer_1_out5, demultiplexer_1_out6, demultiplexer_1_out7,
       demultiplexer_1_out8, demultiplexer_1_out9, demultiplexer_1_out10, demultiplexer_1_out11,
       demultiplexer_1_out12, demultiplexer_1_out13, demultiplexer_1_out14, demultiplexer_1_out15;
  wire [11:0] n12_bit_register_1_q, n12_bit_register_2_q, n12_bit_register_3_q, n12_bit_register_4_q,
       n12_bit_register_5_q, n12_bit_register_6_q, n12_bit_register_7_q, n12_bit_register_8_q,
       n12_bit_register_9_q, n12_bit_register_10_q, n12_bit_register_11_q, n12_bit_register_12_q,
       n12_bit_register_13_q, n12_bit_register_14_q, n12_bit_register_15_q, n12_bit_register_16_q;

  Demultiplexer #(.select(4)) demultiplexer_1 (
    .out0(demultiplexer_1_out0), .out1(demultiplexer_1_out1), .out2(demultiplexer_1_out2),
    .out3(demultiplexer_1_out3), .out4(demultiplexer_1_out4), .out5(demultiplexer_1_out5),
    .out6(demultiplexer_1_out6), .out7(demultiplexer_1_out7), .out8(demultiplexer_1_out8),
    .out9(demultiplexer_1_out9), .out10(demultiplexer_1_out10), .out11(demultiplexer_1_out11),
    .out12(demultiplexer_1_out12), .out13(demultiplexer_1_out13), .out14(demultiplexer_1_out14),
    .out15(demultiplexer_1_out15), .in(write), .sel(rtarget));  // open: en
  Clock clock (.out(clock_out));
  _12_bit_register u_12_bit_register_1 (
    .Q(n12_bit_register_1_q), .D(data), .reset(1'b1), .enable_write(demultiplexer_1_out0), .clock(clock_out));
  _12_bit_register u_12_bit_register_2 (
    .Q(n12_bit_register_2_q), .D(data), .reset(reset), .enable_write(demultiplexer_1_out1), .clock(clock_out));
  _12_bit_register u_12_bit_register_3 (
    .Q(n12_bit_register_3_q), .D(data), .reset(reset), .enable_write(demultiplexer_1_out2), .clock(clock_out));
  _12_bit_register u_12_bit_register_4 (
    .Q(n12_bit_register_4_q), .D(data), .reset(reset), .enable_write(demultiplexer_1_out3), .clock(clock_out));
  _12_bit_register u_12_bit_register_5 (
    .Q(n12_bit_register_5_q), .D(data), .reset(reset), .enable_write(demultiplexer_1_out4), .clock(clock_out));
  _12_bit_register u_12_bit_register_6 (
    .Q(n12_bit_register_6_q), .D(data), .reset(reset), .enable_write(demultiplexer_1_out5), .clock(clock_out));
  _12_bit_register u_12_bit_register_7 (
    .Q(n12_bit_register_7_q), .D(data), .reset(reset), .enable_write(demultiplexer_1_out6), .clock(clock_out));
  _12_bit_register u_12_bit_register_8 (
    .Q(n12_bit_register_8_q), .D(data), .reset(reset), .enable_write(demultiplexer_1_out7), .clock(reset));
  _12_bit_register u_12_bit_register_9 (
    .Q(n12_bit_register_9_q), .D(data), .reset(reset), .enable_write(demultiplexer_1_out8), .clock(clock_out));
  _12_bit_register u_12_bit_register_10 (
    .Q(n12_bit_register_10_q), .D(data), .reset(reset), .enable_write(demultiplexer_1_out9), .clock(clock_out));
  _12_bit_register u_12_bit_register_11 (
    .Q(n12_bit_register_11_q), .D(data), .reset(reset), .enable_write(demultiplexer_1_out10),
    .clock(clock_out));
  _12_bit_register u_12_bit_register_12 (
    .Q(n12_bit_register_12_q), .D(data), .reset(reset), .enable_write(demultiplexer_1_out11),
    .clock(clock_out));
  _12_bit_register u_12_bit_register_13 (
    .Q(n12_bit_register_13_q), .D(data), .reset(reset), .enable_write(demultiplexer_1_out12),
    .clock(clock_out));
  _12_bit_register u_12_bit_register_14 (
    .Q(n12_bit_register_14_q), .D(data), .reset(reset), .enable_write(demultiplexer_1_out13),
    .clock(clock_out));
  _12_bit_register u_12_bit_register_15 (
    .Q(n12_bit_register_15_q), .D(data), .reset(reset), .enable_write(demultiplexer_1_out14),
    .clock(clock_out));
  _12_bit_register u_12_bit_register_16 (
    .Q(n12_bit_register_16_q), .D(data), .reset(reset), .enable_write(demultiplexer_1_out15),
    .clock(clock_out));
  Multiplexer #(.select(4), .width(12)) multiplexer_1 (
    .in0(n12_bit_register_1_q), .in1(n12_bit_register_2_q), .in2(n12_bit_register_3_q),
    .in3(n12_bit_register_4_q), .in4(n12_bit_register_5_q), .in5(n12_bit_register_6_q),
    .in6(n12_bit_register_7_q), .in7(n12_bit_register_8_q), .in8(n12_bit_register_9_q),
    .in9(n12_bit_register_10_q), .in10(n12_bit_register_11_q), .in11(n12_bit_register_12_q),
    .in12(n12_bit_register_13_q), .in13(n12_bit_register_14_q), .in14(n12_bit_register_15_q),
    .in15(n12_bit_register_16_q), .out(out_7), .sel(rSource));  // open: en
  Multiplexer #(.select(4), .width(12)) multiplexer_2 (
    .in0(n12_bit_register_1_q), .in1(n12_bit_register_2_q), .in2(n12_bit_register_3_q),
    .in3(n12_bit_register_4_q), .in4(n12_bit_register_5_q), .in5(n12_bit_register_6_q),
    .in6(n12_bit_register_7_q), .in7(n12_bit_register_8_q), .in8(n12_bit_register_9_q),
    .in9(n12_bit_register_10_q), .in10(n12_bit_register_11_q), .in11(n12_bit_register_12_q),
    .in12(n12_bit_register_13_q), .in13(n12_bit_register_14_q), .in14(n12_bit_register_15_q),
    .in15(n12_bit_register_16_q), .out(out_8), .sel(rDestination));  // open: en
endmodule

module _12_bit_register (
  input  [11:0] D,
  input  reset,
  input  enable_write,
  input  clock,
  output [11:0] Q
);

  D_Flip_Flop #(.trigger("falling")) d_ff_1 (
    .clk(clock), .D(D[0]), .Q(Q[0]), .en(enable_write), .reset(reset));  // open: Qn, preset
  D_Flip_Flop #(.trigger("falling")) d_ff_2 (
    .clk(clock), .D(D[1]), .Q(Q[1]), .en(enable_write), .reset(reset));  // open: Qn, preset
  D_Flip_Flop #(.trigger("falling")) d_ff_3 (
    .clk(clock), .D(D[2]), .Q(Q[2]), .en(enable_write), .reset(reset));  // open: Qn, preset
  D_Flip_Flop #(.trigger("falling")) d_ff_4 (
    .clk(clock), .D(D[3]), .Q(Q[3]), .en(enable_write), .reset(reset));  // open: Qn, preset
  D_Flip_Flop #(.trigger("falling")) d_ff_5 (
    .clk(clock), .D(D[4]), .Q(Q[4]), .en(enable_write), .reset(reset));  // open: Qn, preset
  D_Flip_Flop #(.trigger("falling")) d_ff_6 (
    .clk(clock), .D(D[5]), .Q(Q[5]), .en(enable_write), .reset(reset));  // open: Qn, preset
  D_Flip_Flop #(.trigger("falling")) d_ff_7 (
    .clk(clock), .D(D[6]), .Q(Q[6]), .en(enable_write), .reset(reset));  // open: Qn, preset
  D_Flip_Flop #(.trigger("falling")) d_ff_8 (
    .clk(clock), .D(D[7]), .Q(Q[7]), .en(enable_write), .reset(reset));  // open: Qn, preset
  D_Flip_Flop #(.trigger("falling")) d_ff_9 (
    .clk(clock), .D(D[8]), .Q(Q[8]), .en(enable_write), .reset(reset));  // open: Qn, preset
  D_Flip_Flop #(.trigger("falling")) d_ff_10 (
    .clk(clock), .D(D[9]), .Q(Q[9]), .en(enable_write), .reset(reset));  // open: Qn, preset
  D_Flip_Flop #(.trigger("falling")) d_ff_11 (
    .clk(clock), .D(D[10]), .Q(Q[10]), .en(enable_write), .reset(reset));  // open: Qn, preset
  D_Flip_Flop #(.trigger("falling")) d_ff_12 (
    .clk(clock), .D(D[11]), .Q(Q[11]), .en(enable_write), .reset(reset));  // open: Qn, preset
endmodule

module counter (
  input  clock,
  input  [11:0] D,
  output [11:0] out_3
);

  wire comparator_1_eq, comparator_1_gt, or_1_out;
  wire [11:0] n12_bit_carry_lookahead_adder_1_out_4;

  _12_bit_carry_lookahead__adder u_12_bit_carry_lookahead_adder_1 (
    .in_1(out_3), .in_3({12{1'b0}}), .out_4(n12_bit_carry_lookahead_adder_1_out_4), .carryin(1'b1));  // open: overflow
  _12_bit_register u_12_bit_register_1 (
    .Q(out_3), .D(n12_bit_carry_lookahead_adder_1_out_4), .reset(or_1_out), .enable_write(1'b1), .clock(clock));
  Comparator #(.width(12)) comparator_1 (.a(out_3), .b(D), .gt(comparator_1_gt), .eq(comparator_1_eq));  // open: lt
  or or_1 (or_1_out, comparator_1_gt, comparator_1_eq);
endmodule

module clock_divider (
  input  clock,
  input  [11:0] in_2,
  output out_3
);

  wire comparator_1_eq, d_ff_1_qn;
  wire [11:0] counter_1_out_3;

  counter counter_1 (.clock(clock), .D(in_2), .out_3(counter_1_out_3));
  Comparator #(.width(12)) comparator_1 (.a(counter_1_out_3), .b({12{1'b0}}), .eq(comparator_1_eq));  // open: gt, lt
  D_Flip_Flop #(.trigger("falling")) d_ff_1 (
    .clk(comparator_1_eq), .D(d_ff_1_qn), .Q(out_3), .Qn(d_ff_1_qn));  // open: preset, en, reset

  // Notes on the sheet:
  //   01 = /2
  //   10 = /4
  //   11 = /6
  //   100 = /8
endmodule

module finite_state_machine (
);

  wire and_1_out, and_2_out, and_3_out, and_4_out, and_5_out, and_6_out, and_7_out, and_8_out, clock_1_out,
       comparator_1_eq, comparator_2_eq, comparator_3_eq, comparator_4_eq, comparator_5_eq, comparator_6_eq,
       d_ff_1_qn, d_ff_2_q, d_ff_2_qn, d_ff_3_q, d_ff_3_qn, d_ff_4_q, d_ff_4_qn, d_ff_5_q, d_ff_5_qn,
       d_ff_6_q, d_ff_6_qn, d_ff_7_q, d_ff_7_qn, or_1_out, or_2_out, or_3_out, or_4_out, or_5_out, or_6_out,
       or_7_out, xnor_1_out, xnor_2_out, xnor_3_out, xnor_4_out, xnor_5_out, xnor_6_out, xnor_7_out,
       xnor_8_out;
  wire [11:0] counter_1_out_3, counter_2_out_3, counter_3_out_3, counter_4_out_3, counter_5_out_3,
       counter_6_out_3;

  Clock clock_1 (.out(clock_1_out));
  and and_1 (and_1_out, clock_1_out, d_ff_2_q);
  and and_2 (and_2_out, clock_1_out, d_ff_3_q);
  and and_3 (and_3_out, clock_1_out, d_ff_4_q);
  and and_4 (and_4_out, clock_1_out, d_ff_5_q);
  and and_5 (and_5_out, clock_1_out, d_ff_6_q);
  and and_6 (and_6_out, clock_1_out, d_ff_7_q);
  and and_7 (and_7_out, clock_1_out, d_ff_1_qn);
  D_Flip_Flop d_ff_1 (.clk(and_7_out), .D(d_ff_1_qn), .Qn(d_ff_1_qn));  // open: Q, preset, en, reset
  counter counter_1 (.clock(xnor_1_out), .D(12'ha), .out_3(counter_1_out_3));
  xnor xnor_1 (xnor_1_out, and_1_out, comparator_1_eq);
  counter counter_2 (.clock(xnor_2_out), .D(12'h6), .out_3(counter_2_out_3));
  xnor xnor_2 (xnor_2_out, and_2_out, comparator_2_eq);
  counter counter_3 (.clock(xnor_3_out), .D(12'h4), .out_3(counter_3_out_3));
  xnor xnor_3 (xnor_3_out, and_3_out, comparator_3_eq);
  counter counter_4 (.clock(xnor_4_out), .D(12'ha), .out_3(counter_4_out_3));
  xnor xnor_4 (xnor_4_out, and_4_out, comparator_4_eq);
  counter counter_5 (.clock(xnor_5_out), .D(12'h6), .out_3(counter_5_out_3));
  xnor xnor_5 (xnor_5_out, and_5_out, comparator_5_eq);
  counter counter_6 (.clock(xnor_6_out), .D(12'h4), .out_3(counter_6_out_3));
  xnor xnor_6 (xnor_6_out, and_6_out, comparator_6_eq);
  and and_8 (and_8_out, clock_1_out, d_ff_1_qn);
  Comparator #(.width(12)) comparator_1 (.a(counter_1_out_3), .b(12'h9), .eq(comparator_1_eq));  // open: gt, lt
  Comparator #(.width(12)) comparator_2 (.a(counter_2_out_3), .b(12'h5), .eq(comparator_2_eq));  // open: gt, lt
  Comparator #(.width(12)) comparator_3 (.a(counter_3_out_3), .b(12'h3), .eq(comparator_3_eq));  // open: gt, lt
  Comparator #(.width(12)) comparator_4 (.a(counter_4_out_3), .b(12'h9), .eq(comparator_4_eq));  // open: gt, lt
  Comparator #(.width(12)) comparator_5 (.a(counter_5_out_3), .b(12'h5), .eq(comparator_5_eq));  // open: gt, lt
  Comparator #(.width(12)) comparator_6 (.a(counter_6_out_3), .b(12'h3), .eq(comparator_6_eq));  // open: gt, lt
  or or_1 (or_1_out, comparator_1_eq, comparator_6_eq);
  or or_2 (or_2_out, and_8_out, or_1_out);
  D_Flip_Flop d_ff_2 (.clk(or_2_out), .D(d_ff_2_qn), .Q(d_ff_2_q), .Qn(d_ff_2_qn));  // open: preset, en, reset
  or or_3 (or_3_out, comparator_2_eq, comparator_1_eq);
  D_Flip_Flop d_ff_3 (.clk(or_3_out), .D(d_ff_3_qn), .Q(d_ff_3_q), .Qn(d_ff_3_qn));  // open: preset, en, reset
  or or_4 (or_4_out, comparator_3_eq, comparator_2_eq);
  D_Flip_Flop d_ff_4 (.clk(or_4_out), .D(d_ff_4_qn), .Q(d_ff_4_q), .Qn(d_ff_4_qn));  // open: preset, en, reset
  or or_5 (or_5_out, comparator_4_eq, comparator_3_eq);
  D_Flip_Flop d_ff_5 (.clk(or_5_out), .D(d_ff_5_qn), .Q(d_ff_5_q), .Qn(d_ff_5_qn));  // open: preset, en, reset
  D_Flip_Flop d_ff_6 (.clk(or_6_out), .D(d_ff_6_qn), .Q(d_ff_6_q), .Qn(d_ff_6_qn));  // open: preset, en, reset
  or or_6 (or_6_out, comparator_5_eq, comparator_4_eq);
  or or_7 (or_7_out, comparator_6_eq, comparator_5_eq);
  D_Flip_Flop d_ff_7 (.clk(or_7_out), .D(d_ff_7_qn), .Q(d_ff_7_q), .Qn(d_ff_7_qn));  // open: preset, en, reset
  LED led_1 (.in(xnor_7_out));
  xnor xnor_7 (xnor_7_out, d_ff_2_q, d_ff_3_q);
  LED led_2 (.in(d_ff_3_q));
  LED led_3 (.in(d_ff_2_q));
  LED led_4 (.in(xnor_8_out));
  xnor xnor_8 (xnor_8_out, d_ff_5_q, d_ff_6_q);
  LED led_5 (.in(d_ff_6_q));
  LED led_6 (.in(d_ff_5_q));
endmodule
