// Logisim project ALU_Group16.circ as structural Verilog: 2 circuits, main circuit main
module main (
  input  klok,
  output halt,
  output [6:0] counter,
  output [3:0] op,
  output [11:0] a,
  output [11:0] b,
  output [11:0] oracle,
  output [11:0] result,
  output err_oracle,
  output error,
  output ok,
  output start_delimiter
);

  wire and_1_out, and_2_out, comparator_1_eq, comparator_2_eq;

  Counter #(.width(7), .max('h7f), .trigger("falling")) counter_1 (
    .Q(counter), .carry(halt), .clk(klok));  // open: load, D, count, clr
  RAM #(.addrWidth(10), .dataWidth(4), .bus("separate")) ram_1 (
    .addr({counter, 3'b000}), .data(op), .ld(1'b1));  // open: din, str, sel, clk, clr
  RAM #(.addrWidth(10), .dataWidth(12), .bus("separate")) ram_2 (
    .addr({counter, 3'b001}), .data(a), .ld(1'b1));  // open: din, str, sel, clk, clr
  RAM #(.addrWidth(10), .dataWidth(12), .bus("separate")) ram_3 (
    .addr({counter, 3'b010}), .data(b), .ld(1'b1));  // open: din, str, sel, clk, clr
  RAM #(.addrWidth(10), .dataWidth(12), .bus("separate")) ram_4 (
    .addr({counter, 3'b011}), .data(oracle), .ld(1'b1));  // open: din, str, sel, clk, clr
  RAM #(.addrWidth(10), .dataWidth(1), .bus("separate")) ram_5 (
    .addr({counter, 3'b100}), .data(err_oracle), .ld(1'b1));  // open: din, str, sel, clk, clr
  RAM #(.addrWidth(10), .dataWidth(1), .bus("separate")) ram_6 (
    .addr({counter, 3'b101}), .data(start_delimiter), .ld(1'b1));  // open: din, str, sel, clk, clr
  _12_bit_ALU u_12_bit_alu_1 (.ALU_code(op), .a(a), .b(b), .overflow(error), .result(result));
  Comparator #(.width(1), .mode("unsigned")) comparator_1 (
    .a(error), .b(err_oracle), .eq(comparator_1_eq));  // open: gt, lt
  Comparator #(.width(12)) comparator_2 (.a(result), .b(oracle), .eq(comparator_2_eq));  // open: gt, lt
  and and_1 (and_1_out, comparator_1_eq, error);
  and and_2 (and_2_out, comparator_2_eq, comparator_1_eq, ~error);  // AND_Gate
  or or_1 (ok, and_1_out, and_2_out);

  // Notes on the sheet:
  //   You must complete the circuit '16-bit ALU' instead.
  //   DO NOT EDIT THIS CIRCUIT!
endmodule

module _12_bit_ALU (
  input  [11:0] a,
  input  [11:0] b,
  input  [3:0] ALU_code,
  output overflow,
  output [11:0] result
);

  wire multiplexer_1_out, n12_bit_carry_lookahead_adder_1_overflow, n12_bit_carry_lookahead_adder_2_overflow,
       n12_bit_carry_lookahead_adder_4_overflow, not_1_out, not_2_out, not_3_out, not_4_out, not_5_out,
       not_6_out, not_7_out, not_8_out, not_9_out, not_10_out, not_11_out, not_12_out, not_13_out;
  wire [0:0] and_1_out, not_15_out;
  wire [11:0] and_2_out, multiplexer_2_out, n12_bit_carry_lookahead_adder_1_out_4,
       n12_bit_carry_lookahead_adder_2_out_4, n12_bit_carry_lookahead_adder_3_out_4,
       n12_bit_carry_lookahead_adder_4_out_4, not_14_out, not_16_out, not_17_out, or_1_out;

  Multiplexer multiplexer_1 (.in0(a[10]), .in1(not_1_out), .out(multiplexer_1_out), .sel(a[11]));  // open: en
  not not_1 (not_1_out, a[10]);
  not not_2 (not_2_out, n12_bit_carry_lookahead_adder_4_out_4[0]);
  not not_3 (not_3_out, n12_bit_carry_lookahead_adder_4_out_4[1]);
  not not_4 (not_4_out, n12_bit_carry_lookahead_adder_4_out_4[2]);
  not not_5 (not_5_out, n12_bit_carry_lookahead_adder_4_out_4[3]);
  not not_6 (not_6_out, n12_bit_carry_lookahead_adder_4_out_4[4]);
  not not_7 (not_7_out, n12_bit_carry_lookahead_adder_4_out_4[5]);
  not not_8 (not_8_out, n12_bit_carry_lookahead_adder_4_out_4[6]);
  and and_1 (and_1_out[0], not_2_out, not_3_out, not_4_out, not_5_out, not_6_out, not_7_out, not_8_out, not_9_out, not_10_out, not_11_out, not_12_out, not_13_out, 1'b1);
  not not_9 (not_9_out, n12_bit_carry_lookahead_adder_4_out_4[7]);
  not not_10 (not_10_out, n12_bit_carry_lookahead_adder_4_out_4[8]);
  not not_11 (not_11_out, n12_bit_carry_lookahead_adder_4_out_4[9]);
  not not_12 (not_12_out, n12_bit_carry_lookahead_adder_4_out_4[10]);
  not not_13 (not_13_out, n12_bit_carry_lookahead_adder_4_out_4[11]);
  _12_bit_carry_lookahead__adder u_12_bit_carry_lookahead_adder_1 (
    .in_1({12{1'b0}}), .in_3(not_16_out), .out_4(n12_bit_carry_lookahead_adder_1_out_4),
    .overflow(n12_bit_carry_lookahead_adder_1_overflow), .carryin(1'b1));
  _12_bit_carry_lookahead__adder u_12_bit_carry_lookahead_adder_2 (
    .in_1(b), .in_3(a), .out_4(n12_bit_carry_lookahead_adder_2_out_4),
    .overflow(n12_bit_carry_lookahead_adder_2_overflow), .carryin(1'b0));
  _12_bit_carry_lookahead__adder u_12_bit_carry_lookahead_adder_3 (
    .in_1({12{1'b0}}), .in_3(not_14_out), .out_4(n12_bit_carry_lookahead_adder_3_out_4), .carryin(1'b1));  // open: overflow
  _12_bit_carry_lookahead__adder u_12_bit_carry_lookahead_adder_4 (
    .in_1(n12_bit_carry_lookahead_adder_3_out_4), .in_3(a), .out_4(n12_bit_carry_lookahead_adder_4_out_4),
    .overflow(n12_bit_carry_lookahead_adder_4_overflow), .carryin(1'b0));
  assign not_14_out = ~b;  // NOT_Gate not_14, 12 bits wide
  not not_15 (not_15_out[0], n12_bit_carry_lookahead_adder_4_out_4[11]);
  Multiplexer #(.width(12)) multiplexer_2 (
    .in0({{11{1'b0}}, not_15_out[0]}), .in1({12{1'b0}}), .out(multiplexer_2_out), .sel(and_1_out[0]));  // open: en
  assign not_16_out = ~a;  // NOT_Gate not_16, 12 bits wide
  assign and_2_out = a & b;  // AND_Gate and_2, 12 bits wide
  assign or_1_out = a | b;  // OR_Gate or_1, 12 bits wide
  Multiplexer #(.select(4)) multiplexer_3 (
    .in0(1'b0), .in1(1'b0), .in2(1'b0), .in3(1'b0), .in4(n12_bit_carry_lookahead_adder_1_overflow),
    .in5(n12_bit_carry_lookahead_adder_2_overflow), .in6(n12_bit_carry_lookahead_adder_4_overflow),
    .in7(multiplexer_1_out), .in8(1'b0), .in9(1'b0), .in10(1'b0), .in11(1'b0), .out(overflow), .sel(ALU_code));  // open: in12, in13, in14, in15, en
  assign not_17_out = ~a;  // NOT_Gate not_17, 12 bits wide
  Multiplexer #(.select(4), .width(12)) multiplexer_4 (
    .in0({12{1'b0}}), .in1(and_2_out), .in2(or_1_out), .in3(not_17_out),
    .in4(n12_bit_carry_lookahead_adder_1_out_4), .in5(n12_bit_carry_lookahead_adder_2_out_4),
    .in6(n12_bit_carry_lookahead_adder_4_out_4), .in7({a[11], a[9:0], 1'b0}), .in8({{2{a[11]}}, a[10:1]}),
    .in9({{11{1'b0}}, n12_bit_carry_lookahead_adder_4_out_4[11]}), .in10(multiplexer_2_out),
    .in11({{11{1'b0}}, and_1_out[0]}), .out(result), .sel(ALU_code));  // open: in12, in13, in14, in15, en

  // Notes on the sheet:
  //   This circuit is used as a block in the main circuit, and its layout must remain unchanged. The circuit called "main" should be the main circuit of this file.
  //   numeric addition
  //   numeric substraction
  //   signed shift left
  //   signed shift right
  //   greater than
  //   equal
  //   numeric invers
  //   less than
  //   Do not change the circuit appearance.
  //   DO NOT CHANGE THE INPUTS AND OUTPUTS OF THIS CIRCUIT!
  //   and
  //   Do not add/remove inputs or outputs. Do not even change their location or orientation.
  //   or
endmodule
