// Logisim project project1.circ as structural Verilog
module main (
  input  in_1,
  input  in_2,
  output out_3
);

  wire and_1_out;

  and and_1 (and_1_out, in_1, in_2, in_2);
  not not_1 (out_3, and_1_out);
endmodule

module oef_4 (
  input  A,
  input  B,
  input  C,
  output X,
  output Y
);

  wire and_1_out, and_2_out;

  and and_1 (and_1_out, A, C);
  and and_2 (and_2_out, B, C);
  or or_1 (X, B, B, and_1_out);
  or or_2 (Y, and_1_out, and_2_out, and_2_out);
endmodule

module oef5 (
);

  wire [6:0] keyboard_1_data;

  Keyboard keyboard_1 (.data(keyboard_1_data));  // open: clk, re, clr, avail
  Hex_Digit_Display hex_digit_display_1 (.value({1'b0, keyboard_1_data[6:4]}));  // open: dp
  Hex_Digit_Display hex_digit_display_2 (.value(keyboard_1_data[3:0]));  // open: dp
endmodule

module oef6 (
  input  in_1,
  input  in_2,
  input  in_3
);

  wire n6_4_1_out_4, oef6_1_1_out_4, oef6_2_1_out_4, oef6_3_1_out_4, oef6_5_1_out_4, oef6_6_1_out_4,
       oef6_7_1_out_4;

  oef6_1 oef6_1_1 (.in_1(in_1), .in_2(in_2), .in_3(in_3), .out_4(oef6_1_1_out_4));
  oef6_2 oef6_2_1 (.in_1(in_1), .in_2(in_2), .in_3(in_3), .out_4(oef6_2_1_out_4));
  oef6_3 oef6_3_1 (.in_1(in_1), .in_2(in_2), .in_3(in_3), .out_4(oef6_3_1_out_4));
  _6_4 u_6_4_1 (.in_1(in_1), .in_2(in_2), .in_3(in_3), .out_4(n6_4_1_out_4));
  oef6_5 oef6_5_1 (.in_1(in_1), .in_2(in_2), .in_3(in_3), .out_4(oef6_5_1_out_4));
  oef6_6 oef6_6_1 (.in_1(in_1), .in_2(in_2), .in_3(in_3), .out_4(oef6_6_1_out_4));
  oef6_7 oef6_7_1 (.in_1(in_1), .in_2(in_2), .in_3(in_3), .out_4(oef6_7_1_out_4));
  _7_Segment_Display u_7_segment_display_1 (
    .g(oef6_7_1_out_4), .f(oef6_1_1_out_4), .a(oef6_6_1_out_4), .b(oef6_5_1_out_4), .e(oef6_2_1_out_4),
    .d(oef6_3_1_out_4), .c(n6_4_1_out_4));  // open: dp
endmodule

module oef6_2 (
  input  in_1,
  input  in_2,
  input  in_3,
  output out_4
);

  wire and_1_out, and_2_out, not_1_out, not_2_out, not_3_out, or_1_out, or_2_out;

  not not_1 (not_1_out, or_1_out);
  or or_1 (or_1_out, in_1, in_2, in_3);
  and and_1 (and_1_out, in_1, in_2, in_3);
  and and_2 (and_2_out, in_2, not_2_out, not_2_out);
  not not_2 (not_2_out, in_3);
  or or_2 (or_2_out, not_1_out, not_1_out, and_2_out, and_2_out);
  not not_3 (not_3_out, and_1_out);
  and and_3 (out_4, or_2_out, or_2_out, not_3_out);
endmodule

module oef6_1 (
  input  in_1,
  input  in_2,
  input  in_3,
  output out_4
);

  wire and_1_out, and_2_out, not_1_out, not_2_out, or_1_out;

  and and_1 (and_1_out, in_1, in_2, in_3);
  not not_1 (not_1_out, and_1_out);
  not not_2 (not_2_out, or_1_out);
  or or_1 (or_1_out, in_1, in_2, in_3);
  and and_2 (and_2_out, in_1, not_1_out);
  or or_2 (out_4, and_2_out, not_2_out);
endmodule

module oef6_7 (
  input  in_1,
  input  in_2,
  input  in_3,
  output out_4
);

  wire and_1_out, and_2_out, not_1_out, not_2_out, not_3_out, or_1_out, or_2_out, or_3_out;

  and and_1 (and_1_out, in_1, in_2, in_3, in_3);
  or or_1 (or_1_out, in_1, in_2, in_3);
  not not_1 (not_1_out, or_1_out);
  or or_2 (or_2_out, and_1_out, not_1_out);
  not not_2 (not_2_out, in_1);
  not not_3 (not_3_out, in_2);
  and and_2 (and_2_out, not_2_out, not_3_out, in_3);
  or or_3 (or_3_out, or_2_out, and_2_out);
  not not_4 (out_4, or_3_out);
endmodule

module oef6_6 (
  input  in_1,
  input  in_2,
  input  in_3,
  output out_4
);

  wire and_1_out, and_2_out, not_1_out, not_2_out, not_3_out, not_4_out, not_5_out, not_6_out;

  not not_1 (not_1_out, in_2);
  not not_2 (not_2_out, in_3);
  not not_3 (not_3_out, in_1);
  not not_4 (not_4_out, in_2);
  and and_1 (and_1_out, in_1, not_1_out, not_2_out);
  and and_2 (and_2_out, not_3_out, not_4_out, in_3);
  not not_5 (not_5_out, and_1_out);
  not not_6 (not_6_out, and_2_out);
  and and_3 (out_4, not_5_out, not_6_out);
endmodule

module oef6_5 (
  input  in_1,
  input  in_2,
  input  in_3,
  output out_4
);

  wire and_1_out, and_2_out, and_3_out, not_1_out, or_1_out;

  and and_1 (and_1_out, in_1, in_2);
  and and_2 (and_2_out, in_1, in_3);
  and and_3 (and_3_out, in_1, in_3, in_2);
  or or_1 (or_1_out, and_1_out, and_2_out);
  or or_2 (out_4, not_1_out, and_3_out);
  not not_1 (not_1_out, or_1_out);
endmodule

module _6_4 (
  input  in_1,
  input  in_2,
  input  in_3,
  output out_4
);

  wire and_1_out, not_1_out, not_2_out;

  not not_1 (not_1_out, in_1);
  not not_2 (not_2_out, in_3);
  not not_3 (out_4, and_1_out);
  and and_1 (and_1_out, not_1_out, in_2, not_2_out);
endmodule

module oef6_3 (
  input  in_1,
  input  in_2,
  input  in_3,
  output out_4
);

  wire and_1_out, and_2_out, and_3_out, not_1_out, not_2_out, not_3_out, not_4_out, not_5_out, not_6_out,
       not_7_out;

  and and_1 (and_1_out, in_1, not_1_out, not_2_out);
  not not_1 (not_1_out, in_2);
  not not_2 (not_2_out, in_3);
  not not_3 (not_3_out, in_1);
  and and_2 (and_2_out, in_3, not_3_out, not_4_out);
  not not_4 (not_4_out, in_2);
  and and_3 (and_3_out, in_1, in_2, in_3);
  not not_5 (not_5_out, and_3_out);
  not not_6 (not_6_out, and_1_out);
  not not_7 (not_7_out, and_2_out);
  and and_4 (out_4, not_5_out, not_6_out, not_7_out);
endmodule
